# Fritzing sketch weather_dht22 (saved by Fritzing 0.8.7b)
breadboards: 1

parts:
  Part1 = Arduino Uno (Rev3)
  DHT22 = Humidity and Temperature Sensor RHT03

nets:
  N1: Part1.D2, DHT22.Data-signal
  5V: Part1.5V, DHT22.Vcc
  N2: Part1.GND, DHT22.GND_2
